# Fritzing sketch LED8X8-com-arduino-potenciometro (saved by Fritzing 0.9.4)
breadboards: 2

parts:
  Componente2 = Arduino Uno (Rev3)
  R1 = Resistor [tolerance=±5% resistance=220 package="2512 [SMD]"]
  R2 = Resistor [tolerance=±5% resistance=220 package="2512 [SMD]"]
  R3 = Resistor [tolerance=±5% resistance=220 package="2512 [SMD]"]
  R4 = Resistor [tolerance=±5% resistance=220 package="2512 [SMD]"]
  Disp1 = LBT2088AH [part_number=LBT2088AH]
  R5 = Resistor [tolerance=±5% resistance=220 package="2512 [SMD]"]
  R6 = Resistor [tolerance=±5% resistance=220 package="2512 [SMD]"]  # not connected
  R7 = Resistor [tolerance=±5% resistance=220 package="2512 [SMD]"]
  R8 = Resistor [tolerance=±5% resistance=220 package="2512 [SMD]"]  # not connected
  R9 = Resistor [tolerance=±5% resistance=220 package="2512 [SMD]"]
  R10 = Resistor [tolerance=±5% resistance=220 package="2512 [SMD]"]
  U1 = POT [package=pot_mammoth]

nets:
  N1: Componente2.A0, R3.Pin_0
  N2: Componente2.A1, Disp1.pin_6
  N3: Componente2.A2, R4.Pin_0
  N4: Componente2.A3, R5.Pin_0
  N5: Componente2.A4/SDA, U1.A
  N6: Componente2.D8, R10.Pin_1
  N7: Componente2.D9_PWM, Disp1.pin_13
  N8: Componente2.D10_PWM/SS, R9.Pin_1
  N9: Componente2.D11_PWM/MOSI, Disp1.pin_11
  N10: Componente2.D12/MISO, Disp1.pin_10
  N11: Componente2.D13/SCK, R7.Pin_1
  N12: Componente2.GND, U1.S
  N13: Componente2.D2, Disp1.pin_4
  N14: Componente2.D3_PWM, Disp1.pin_3
  N15: Componente2.D4, R2.Pin_0
  N16: Componente2.D5_PWM, R1.Pin_0
  N17: Componente2.D6_PWM, Disp1.pin_16
  N18: Componente2.D7, Disp1.pin_15
  N19: Componente2.5V, U1.E
  N20: R1.Pin_1, Disp1.pin1
  N21: R2.Pin_1, Disp1.pin2
  N22: R3.Pin_1, Disp1.pin_5
  N23: R4.Pin_1, Disp1.pin_7
  N24: Disp1.pin_8, R5.Pin_1
  N25: Disp1.pin_9, R7.Pin_0
  N26: Disp1.pin_12, R9.Pin_0
  N27: Disp1.pin_14, R10.Pin_0
