# Fritzing sketch circuito-jogo-ping-pong (saved by Fritzing 0.9.4)

parts:
  Componente1 = Matrix LED de 8x8 basada en MAX7219
  Componente2 = Arduino Uno (Rev3) - ICSP
  U1 = POT [package=pot_alpha_rv16af-20]

nets:
  VCC: Componente1.VCC, Componente2.5V
  GND: Componente1.GND, Componente2.GND, U1.E
  N1: Componente1.CS, Componente2.D10_PWM/SS
  N2: Componente1.CLK, Componente2.D11_PWM/MOSI
  N3: Componente1.DIN, Componente2.D12/MISO
  N4: Componente1.VCC(OUT), U1.A
  N5: Componente2.A0, U1.S
