# Fritzing sketch Game Ping-Pong (saved by Fritzing 0.9.4)
breadboards: 1

parts:
  Componente1 = LED Matrix - Serial Interface - Red/Green/Blue
  Componente2 = LED Matrix - Serial Interface - Red/Green/Blue
  Componente3 = Arduino Pro Mini (3.3V)
  U2 = POT [package=alps_pot]
  J1 = Piezo Speaker
  R1 = Resistor [tolerance=±5% resistance=220 package="0402 [SMD]"]
  Q1 = NPN-Transistor [package="TO92 [THT]"]
  U3 = SWITCH-SPST-2 [package=switch-spst-vertical]
  BAT1 = BC9VPC [package=bc9vpc]
  Componente4 = FTDI Basic Programmer

nets:
  N1: Componente1.SCK, Componente2.SCK
  N2: Componente1.CS, Componente2.CS
  N3: Componente1.MISO, Componente2.MOSI
  GND: Componente1.GND, Componente2.GND, U2.A, J1.pin2
  N4: Componente1.MOSI, U2.E, Q1.E, BAT1.V-
  N5: Componente3.DTR, Componente4.DTR
  N6: Componente3.TXO, Componente4.RXI
  N7: Componente3.RXI, Componente4.TXO
  N8: Componente3.VCC, Componente4.POWER
  GND_2: Componente3.GND, Componente4.CTS, Componente4.GND
  N9: J1.pin1, Q1.C
  N10: R1.Pin_1, Q1.B
  N11: U3.O, BAT1.V+

notes:
  NPN 2SC1815
  POT 10K
  Buzzer 5v
  Arduino Pro Mini
