# Fritzing sketch controle de servos (saved by Fritzing 0.9.4)
breadboards: 1

parts:
  R1 = Resistor [tolerance=±5% resistance=1.5k package=THT]
  R2 = Resistor [tolerance=±5% resistance=220k package=THT]
  R3 = Resistor [tolerance=±5% resistance=10k package=THT]
  R4 = Resistor [tolerance=±5% resistance=220k package=THT]
  R5 = Resistor [tolerance=±5% resistance=10k package=THT]
  J1 = Basic Servo
  RE1 = Rotary Encoder [package=THT]
  C1 = Ceramic Capacitor [capacitance=100nF voltage=50V package="100 mil [THT, multilayer]"]
  C2 = Electrolytic Capacitor [capacitance=470µF voltage=16V package="100 mil [THT, electrolytic]"]
  U1 = 555 Timer [package="DIP8 [THT]"]
  VCC1 = 4 x AAA Battery Mount
  Q1 = NPN-Transistor [package="TO92 [THT]"]
  J2 = Screw terminal - 2 pins [package=THT]

nets:
  N1: R1.Pin_0, R4.Pin_0, RE1.EncoderPinA
  N2: R1.Pin_1, C1.1, U1.Trigger, U1.Threshold
  N3: R2.Pin_0, R3.Pin_1, R5.Pin_0, J1.vcc, U1.Reset, U1.Vcc_Supply_Voltage, VCC1.+, J2.pin2
  N4: R2.Pin_1, R4.Pin_1, RE1.EncoderPinC, RE1.EncoderPinB, U1.Discharge
  N5: R3.Pin_0, J1.pulse, Q1.C
  N6: R5.Pin_1, Q1.B
  N7: J1.gnd, C1.0, C2.-, U1.Ground, VCC1.-, Q1.E, J2.pin1
  N8: C2.+, U1.Control_Voltage
